// Logisim project 16x4 RAM.circ as structural Verilog: 2 circuits, main circuit main
module main (
  input  [3:0] ADDRESS,
  input  A3,
  input  A2,
  input  A1,
  input  A0,
  output Y3,
  output Y2,
  output Y1,
  output Y0
);

  wire clock_1_out;

  Clock clock_1 (.out(clock_1_out));
  memory memory_1 (
    .CLOCK(clock_1_out), .ADDRESS(ADDRESS), .D3(A3), .D2(A2), .D1(A1), .D0(A0), .OUT_D3(Y3), .OUT_D2(Y2),
    .OUT_D1(Y1), .OUT_D0(Y0));

  // Notes on the sheet:
  //   Clock
endmodule

module memory (
  input  CLOCK,
  input  [3:0] ADDRESS,
  input  D3,
  input  D2,
  input  D1,
  input  D0,
  output OUT_D3,
  output OUT_D2,
  output OUT_D1,
  output OUT_D0
);

  wire d_ff_1_q, d_ff_2_q, d_ff_3_q, d_ff_4_q, d_ff_5_q, d_ff_6_q, d_ff_7_q, d_ff_8_q, d_ff_9_q, d_ff_10_q,
       d_ff_11_q, d_ff_12_q, d_ff_13_q, d_ff_14_q, d_ff_15_q, d_ff_16_q, d_ff_17_q, d_ff_18_q, d_ff_19_q,
       d_ff_20_q, d_ff_21_q, d_ff_22_q, d_ff_23_q, d_ff_24_q, d_ff_25_q, d_ff_26_q, d_ff_27_q, d_ff_28_q,
       d_ff_29_q, d_ff_30_q, d_ff_31_q, d_ff_32_q, d_ff_33_q, d_ff_34_q, d_ff_35_q, d_ff_36_q, d_ff_37_q,
       d_ff_38_q, d_ff_39_q, d_ff_40_q, d_ff_41_q, d_ff_42_q, d_ff_43_q, d_ff_44_q, d_ff_45_q, d_ff_46_q,
       d_ff_47_q, d_ff_48_q, d_ff_49_q, d_ff_50_q, d_ff_51_q, d_ff_52_q, d_ff_53_q, d_ff_54_q, d_ff_55_q,
       d_ff_56_q, d_ff_57_q, d_ff_58_q, d_ff_59_q, d_ff_60_q, d_ff_61_q, d_ff_62_q, d_ff_63_q, d_ff_64_q,
       demultiplexer_1_out0, demultiplexer_1_out1, demultiplexer_1_out2, demultiplexer_1_out3,
       demultiplexer_1_out4, demultiplexer_1_out5, demultiplexer_1_out6, demultiplexer_1_out7,
       demultiplexer_1_out8, demultiplexer_1_out9, demultiplexer_1_out10, demultiplexer_1_out11,
       demultiplexer_1_out12, demultiplexer_1_out13, demultiplexer_1_out14, demultiplexer_1_out15,
       demultiplexer_2_out0, demultiplexer_2_out1, demultiplexer_2_out2, demultiplexer_2_out3,
       demultiplexer_2_out4, demultiplexer_2_out5, demultiplexer_2_out6, demultiplexer_2_out7,
       demultiplexer_2_out8, demultiplexer_2_out9, demultiplexer_2_out10, demultiplexer_2_out11,
       demultiplexer_2_out12, demultiplexer_2_out13, demultiplexer_2_out14, demultiplexer_2_out15,
       demultiplexer_3_out0, demultiplexer_3_out1, demultiplexer_3_out2, demultiplexer_3_out3,
       demultiplexer_3_out4, demultiplexer_3_out5, demultiplexer_3_out6, demultiplexer_3_out7,
       demultiplexer_3_out8, demultiplexer_3_out9, demultiplexer_3_out10, demultiplexer_3_out11,
       demultiplexer_3_out12, demultiplexer_3_out13, demultiplexer_3_out14, demultiplexer_3_out15,
       demultiplexer_4_out0, demultiplexer_4_out1, demultiplexer_4_out2, demultiplexer_4_out3,
       demultiplexer_4_out4, demultiplexer_4_out5, demultiplexer_4_out6, demultiplexer_4_out7,
       demultiplexer_4_out8, demultiplexer_4_out9, demultiplexer_4_out10, demultiplexer_4_out11,
       demultiplexer_4_out12, demultiplexer_4_out13, demultiplexer_4_out14, demultiplexer_4_out15,
       demultiplexer_5_out0, demultiplexer_5_out1, demultiplexer_5_out2, demultiplexer_5_out3,
       demultiplexer_5_out4, demultiplexer_5_out5, demultiplexer_5_out6, demultiplexer_5_out7,
       demultiplexer_5_out8, demultiplexer_5_out9, demultiplexer_5_out10, demultiplexer_5_out11,
       demultiplexer_5_out12, demultiplexer_5_out13, demultiplexer_5_out14, demultiplexer_5_out15;

  Demultiplexer #(.select(4), .enable("false")) demultiplexer_1 (
    .out0(demultiplexer_1_out0), .out1(demultiplexer_1_out1), .out2(demultiplexer_1_out2),
    .out3(demultiplexer_1_out3), .out4(demultiplexer_1_out4), .out5(demultiplexer_1_out5),
    .out6(demultiplexer_1_out6), .out7(demultiplexer_1_out7), .out8(demultiplexer_1_out8),
    .out9(demultiplexer_1_out9), .out10(demultiplexer_1_out10), .out11(demultiplexer_1_out11),
    .out12(demultiplexer_1_out12), .out13(demultiplexer_1_out13), .out14(demultiplexer_1_out14),
    .out15(demultiplexer_1_out15), .in(CLOCK), .sel(ADDRESS));
  Demultiplexer #(.select(4), .enable("false")) demultiplexer_2 (
    .out0(demultiplexer_2_out0), .out1(demultiplexer_2_out1), .out2(demultiplexer_2_out2),
    .out3(demultiplexer_2_out3), .out4(demultiplexer_2_out4), .out5(demultiplexer_2_out5),
    .out6(demultiplexer_2_out6), .out7(demultiplexer_2_out7), .out8(demultiplexer_2_out8),
    .out9(demultiplexer_2_out9), .out10(demultiplexer_2_out10), .out11(demultiplexer_2_out11),
    .out12(demultiplexer_2_out12), .out13(demultiplexer_2_out13), .out14(demultiplexer_2_out14),
    .out15(demultiplexer_2_out15), .in(D3), .sel(ADDRESS));
  Demultiplexer #(.select(4), .enable("false")) demultiplexer_3 (
    .out0(demultiplexer_3_out0), .out1(demultiplexer_3_out1), .out2(demultiplexer_3_out2),
    .out3(demultiplexer_3_out3), .out4(demultiplexer_3_out4), .out5(demultiplexer_3_out5),
    .out6(demultiplexer_3_out6), .out7(demultiplexer_3_out7), .out8(demultiplexer_3_out8),
    .out9(demultiplexer_3_out9), .out10(demultiplexer_3_out10), .out11(demultiplexer_3_out11),
    .out12(demultiplexer_3_out12), .out13(demultiplexer_3_out13), .out14(demultiplexer_3_out14),
    .out15(demultiplexer_3_out15), .in(D2), .sel(ADDRESS));
  Demultiplexer #(.select(4), .enable("false")) demultiplexer_4 (
    .out0(demultiplexer_4_out0), .out1(demultiplexer_4_out1), .out2(demultiplexer_4_out2),
    .out3(demultiplexer_4_out3), .out4(demultiplexer_4_out4), .out5(demultiplexer_4_out5),
    .out6(demultiplexer_4_out6), .out7(demultiplexer_4_out7), .out8(demultiplexer_4_out8),
    .out9(demultiplexer_4_out9), .out10(demultiplexer_4_out10), .out11(demultiplexer_4_out11),
    .out12(demultiplexer_4_out12), .out13(demultiplexer_4_out13), .out14(demultiplexer_4_out14),
    .out15(demultiplexer_4_out15), .in(D1), .sel(ADDRESS));
  Demultiplexer #(.select(4), .enable("false")) demultiplexer_5 (
    .out0(demultiplexer_5_out0), .out1(demultiplexer_5_out1), .out2(demultiplexer_5_out2),
    .out3(demultiplexer_5_out3), .out4(demultiplexer_5_out4), .out5(demultiplexer_5_out5),
    .out6(demultiplexer_5_out6), .out7(demultiplexer_5_out7), .out8(demultiplexer_5_out8),
    .out9(demultiplexer_5_out9), .out10(demultiplexer_5_out10), .out11(demultiplexer_5_out11),
    .out12(demultiplexer_5_out12), .out13(demultiplexer_5_out13), .out14(demultiplexer_5_out14),
    .out15(demultiplexer_5_out15), .in(D0), .sel(ADDRESS));
  D_Flip_Flop d_ff_1 (
    .clk(demultiplexer_1_out0), .D(demultiplexer_2_out0), .Q(d_ff_1_q));  // open: Qn, preset, en, reset
  D_Flip_Flop d_ff_2 (
    .clk(demultiplexer_1_out1), .D(demultiplexer_2_out1), .Q(d_ff_2_q));  // open: Qn, preset, en, reset
  D_Flip_Flop d_ff_3 (
    .clk(demultiplexer_1_out2), .D(demultiplexer_2_out2), .Q(d_ff_3_q));  // open: Qn, preset, en, reset
  D_Flip_Flop d_ff_4 (
    .clk(demultiplexer_1_out3), .D(demultiplexer_2_out3), .Q(d_ff_4_q));  // open: Qn, preset, en, reset
  D_Flip_Flop d_ff_5 (
    .clk(demultiplexer_1_out4), .D(demultiplexer_2_out4), .Q(d_ff_5_q));  // open: Qn, preset, en, reset
  D_Flip_Flop d_ff_6 (
    .clk(demultiplexer_1_out5), .D(demultiplexer_2_out5), .Q(d_ff_6_q));  // open: Qn, preset, en, reset
  D_Flip_Flop d_ff_7 (
    .clk(demultiplexer_1_out6), .D(demultiplexer_2_out6), .Q(d_ff_7_q));  // open: Qn, preset, en, reset
  D_Flip_Flop d_ff_8 (
    .clk(demultiplexer_1_out7), .D(demultiplexer_2_out7), .Q(d_ff_8_q));  // open: Qn, preset, en, reset
  D_Flip_Flop d_ff_9 (
    .clk(demultiplexer_1_out8), .D(demultiplexer_2_out8), .Q(d_ff_9_q));  // open: Qn, preset, en, reset
  D_Flip_Flop d_ff_10 (
    .clk(demultiplexer_1_out9), .D(demultiplexer_2_out9), .Q(d_ff_10_q));  // open: Qn, preset, en, reset
  D_Flip_Flop d_ff_11 (
    .clk(demultiplexer_1_out10), .D(demultiplexer_2_out10), .Q(d_ff_11_q));  // open: Qn, preset, en, reset
  D_Flip_Flop d_ff_12 (
    .clk(demultiplexer_1_out11), .D(demultiplexer_2_out11), .Q(d_ff_12_q));  // open: Qn, preset, en, reset
  D_Flip_Flop d_ff_13 (
    .clk(demultiplexer_1_out12), .D(demultiplexer_2_out12), .Q(d_ff_13_q));  // open: Qn, preset, en, reset
  D_Flip_Flop d_ff_14 (
    .clk(demultiplexer_1_out13), .D(demultiplexer_2_out13), .Q(d_ff_14_q));  // open: Qn, preset, en, reset
  D_Flip_Flop d_ff_15 (
    .clk(demultiplexer_1_out14), .D(demultiplexer_2_out14), .Q(d_ff_15_q));  // open: Qn, preset, en, reset
  D_Flip_Flop d_ff_16 (
    .clk(demultiplexer_1_out15), .D(demultiplexer_2_out15), .Q(d_ff_16_q));  // open: Qn, preset, en, reset
  D_Flip_Flop d_ff_17 (
    .clk(demultiplexer_1_out0), .D(demultiplexer_3_out0), .Q(d_ff_17_q));  // open: Qn, preset, en, reset
  D_Flip_Flop d_ff_18 (
    .clk(demultiplexer_1_out1), .D(demultiplexer_3_out1), .Q(d_ff_18_q));  // open: Qn, preset, en, reset
  D_Flip_Flop d_ff_19 (
    .clk(demultiplexer_1_out2), .D(demultiplexer_3_out2), .Q(d_ff_19_q));  // open: Qn, preset, en, reset
  D_Flip_Flop d_ff_20 (
    .clk(demultiplexer_1_out3), .D(demultiplexer_3_out3), .Q(d_ff_20_q));  // open: Qn, preset, en, reset
  D_Flip_Flop d_ff_21 (
    .clk(demultiplexer_1_out4), .D(demultiplexer_3_out4), .Q(d_ff_21_q));  // open: Qn, preset, en, reset
  D_Flip_Flop d_ff_22 (
    .clk(demultiplexer_1_out5), .D(demultiplexer_3_out6), .Q(d_ff_22_q));  // open: Qn, preset, en, reset
  D_Flip_Flop d_ff_23 (
    .clk(demultiplexer_1_out6), .D(demultiplexer_3_out5), .Q(d_ff_23_q));  // open: Qn, preset, en, reset
  D_Flip_Flop d_ff_24 (
    .clk(demultiplexer_1_out7), .D(demultiplexer_3_out7), .Q(d_ff_24_q));  // open: Qn, preset, en, reset
  D_Flip_Flop d_ff_25 (
    .clk(demultiplexer_1_out8), .D(demultiplexer_3_out8), .Q(d_ff_25_q));  // open: Qn, preset, en, reset
  D_Flip_Flop d_ff_26 (
    .clk(demultiplexer_1_out9), .D(demultiplexer_3_out9), .Q(d_ff_26_q));  // open: Qn, preset, en, reset
  D_Flip_Flop d_ff_27 (
    .clk(demultiplexer_1_out10), .D(demultiplexer_3_out10), .Q(d_ff_27_q));  // open: Qn, preset, en, reset
  D_Flip_Flop d_ff_28 (
    .clk(demultiplexer_1_out11), .D(demultiplexer_3_out11), .Q(d_ff_28_q));  // open: Qn, preset, en, reset
  D_Flip_Flop d_ff_29 (
    .clk(demultiplexer_1_out12), .D(demultiplexer_3_out12), .Q(d_ff_29_q));  // open: Qn, preset, en, reset
  D_Flip_Flop d_ff_30 (
    .clk(demultiplexer_1_out13), .D(demultiplexer_3_out13), .Q(d_ff_30_q));  // open: Qn, preset, en, reset
  D_Flip_Flop d_ff_31 (
    .clk(demultiplexer_1_out14), .D(demultiplexer_3_out14), .Q(d_ff_31_q));  // open: Qn, preset, en, reset
  D_Flip_Flop d_ff_32 (
    .clk(demultiplexer_1_out15), .D(demultiplexer_3_out15), .Q(d_ff_32_q));  // open: Qn, preset, en, reset
  D_Flip_Flop d_ff_33 (
    .clk(demultiplexer_1_out0), .D(demultiplexer_4_out0), .Q(d_ff_33_q));  // open: Qn, preset, en, reset
  D_Flip_Flop d_ff_34 (
    .clk(demultiplexer_1_out1), .D(demultiplexer_4_out1), .Q(d_ff_34_q));  // open: Qn, preset, en, reset
  D_Flip_Flop d_ff_35 (
    .clk(demultiplexer_1_out2), .D(demultiplexer_4_out2), .Q(d_ff_35_q));  // open: Qn, preset, en, reset
  D_Flip_Flop d_ff_36 (
    .clk(demultiplexer_1_out3), .D(demultiplexer_4_out3), .Q(d_ff_36_q));  // open: Qn, preset, en, reset
  D_Flip_Flop d_ff_37 (
    .clk(demultiplexer_1_out4), .D(demultiplexer_4_out4), .Q(d_ff_37_q));  // open: Qn, preset, en, reset
  D_Flip_Flop d_ff_38 (
    .clk(demultiplexer_1_out5), .D(demultiplexer_4_out5), .Q(d_ff_38_q));  // open: Qn, preset, en, reset
  D_Flip_Flop d_ff_39 (
    .clk(demultiplexer_1_out6), .D(demultiplexer_4_out6), .Q(d_ff_39_q));  // open: Qn, preset, en, reset
  D_Flip_Flop d_ff_40 (
    .clk(demultiplexer_1_out7), .D(demultiplexer_4_out7), .Q(d_ff_40_q));  // open: Qn, preset, en, reset
  D_Flip_Flop d_ff_41 (
    .clk(demultiplexer_1_out8), .D(demultiplexer_4_out8), .Q(d_ff_41_q));  // open: Qn, preset, en, reset
  D_Flip_Flop d_ff_42 (
    .clk(demultiplexer_1_out9), .D(demultiplexer_4_out9), .Q(d_ff_42_q));  // open: Qn, preset, en, reset
  D_Flip_Flop d_ff_43 (
    .clk(demultiplexer_1_out10), .D(demultiplexer_4_out10), .Q(d_ff_43_q));  // open: Qn, preset, en, reset
  D_Flip_Flop d_ff_44 (
    .clk(demultiplexer_1_out11), .D(demultiplexer_4_out11), .Q(d_ff_44_q));  // open: Qn, preset, en, reset
  D_Flip_Flop d_ff_45 (
    .clk(demultiplexer_1_out12), .D(demultiplexer_4_out12), .Q(d_ff_45_q));  // open: Qn, preset, en, reset
  D_Flip_Flop d_ff_46 (
    .clk(demultiplexer_1_out13), .D(demultiplexer_4_out13), .Q(d_ff_46_q));  // open: Qn, preset, en, reset
  D_Flip_Flop d_ff_47 (
    .clk(demultiplexer_1_out14), .D(demultiplexer_4_out14), .Q(d_ff_47_q));  // open: Qn, preset, en, reset
  D_Flip_Flop d_ff_48 (
    .clk(demultiplexer_1_out15), .D(demultiplexer_4_out15), .Q(d_ff_48_q));  // open: Qn, preset, en, reset
  D_Flip_Flop d_ff_49 (
    .clk(demultiplexer_1_out0), .D(demultiplexer_5_out0), .Q(d_ff_49_q));  // open: Qn, preset, en, reset
  D_Flip_Flop d_ff_50 (
    .clk(demultiplexer_1_out1), .D(demultiplexer_5_out1), .Q(d_ff_50_q));  // open: Qn, preset, en, reset
  D_Flip_Flop d_ff_51 (
    .clk(demultiplexer_1_out2), .D(demultiplexer_5_out2), .Q(d_ff_51_q));  // open: Qn, preset, en, reset
  D_Flip_Flop d_ff_52 (
    .clk(demultiplexer_1_out3), .D(demultiplexer_5_out3), .Q(d_ff_52_q));  // open: Qn, preset, en, reset
  D_Flip_Flop d_ff_53 (
    .clk(demultiplexer_1_out4), .D(demultiplexer_5_out4), .Q(d_ff_53_q));  // open: Qn, preset, en, reset
  D_Flip_Flop d_ff_54 (
    .clk(demultiplexer_1_out5), .D(demultiplexer_5_out5), .Q(d_ff_54_q));  // open: Qn, preset, en, reset
  D_Flip_Flop d_ff_55 (
    .clk(demultiplexer_1_out6), .D(demultiplexer_5_out6), .Q(d_ff_55_q));  // open: Qn, preset, en, reset
  D_Flip_Flop d_ff_56 (
    .clk(demultiplexer_1_out7), .D(demultiplexer_5_out7), .Q(d_ff_56_q));  // open: Qn, preset, en, reset
  D_Flip_Flop d_ff_57 (
    .clk(demultiplexer_1_out8), .D(demultiplexer_5_out8), .Q(d_ff_57_q));  // open: Qn, preset, en, reset
  D_Flip_Flop d_ff_58 (
    .clk(demultiplexer_1_out9), .D(demultiplexer_5_out9), .Q(d_ff_58_q));  // open: Qn, preset, en, reset
  D_Flip_Flop d_ff_59 (
    .clk(demultiplexer_1_out10), .D(demultiplexer_5_out10), .Q(d_ff_59_q));  // open: Qn, preset, en, reset
  D_Flip_Flop d_ff_60 (
    .clk(demultiplexer_1_out11), .D(demultiplexer_5_out11), .Q(d_ff_60_q));  // open: Qn, preset, en, reset
  D_Flip_Flop d_ff_61 (
    .clk(demultiplexer_1_out12), .D(demultiplexer_5_out12), .Q(d_ff_61_q));  // open: Qn, preset, en, reset
  D_Flip_Flop d_ff_62 (
    .clk(demultiplexer_1_out13), .D(demultiplexer_5_out13), .Q(d_ff_62_q));  // open: Qn, preset, en, reset
  D_Flip_Flop d_ff_63 (
    .clk(demultiplexer_1_out14), .D(demultiplexer_5_out14), .Q(d_ff_63_q));  // open: Qn, preset, en, reset
  D_Flip_Flop d_ff_64 (
    .clk(demultiplexer_1_out15), .D(demultiplexer_5_out15), .Q(d_ff_64_q));  // open: Qn, preset, en, reset
  Multiplexer #(.select(4), .enable("false")) multiplexer_1 (
    .in0(d_ff_1_q), .in1(d_ff_2_q), .in2(d_ff_3_q), .in3(d_ff_4_q), .in4(d_ff_5_q), .in5(d_ff_6_q),
    .in6(d_ff_7_q), .in7(d_ff_8_q), .in8(d_ff_9_q), .in9(d_ff_10_q), .in10(d_ff_11_q), .in11(d_ff_12_q),
    .in12(d_ff_13_q), .in13(d_ff_14_q), .in14(d_ff_15_q), .in15(d_ff_16_q), .out(OUT_D3), .sel(ADDRESS));
  Multiplexer #(.select(4), .enable("false")) multiplexer_2 (
    .in0(d_ff_17_q), .in1(d_ff_18_q), .in2(d_ff_19_q), .in3(d_ff_20_q), .in4(d_ff_21_q), .in5(d_ff_22_q),
    .in6(d_ff_23_q), .in7(d_ff_24_q), .in8(d_ff_25_q), .in9(d_ff_26_q), .in10(d_ff_27_q), .in11(d_ff_28_q),
    .in12(d_ff_29_q), .in13(d_ff_30_q), .in14(d_ff_31_q), .in15(d_ff_32_q), .out(OUT_D2), .sel(ADDRESS));
  Multiplexer #(.select(4), .enable("false")) multiplexer_3 (
    .in0(d_ff_33_q), .in1(d_ff_34_q), .in2(d_ff_35_q), .in3(d_ff_36_q), .in4(d_ff_37_q), .in5(d_ff_38_q),
    .in6(d_ff_39_q), .in7(d_ff_40_q), .in8(d_ff_43_q), .in9(d_ff_41_q), .in10(d_ff_42_q), .in11(d_ff_44_q),
    .in12(d_ff_45_q), .in13(d_ff_46_q), .in14(d_ff_47_q), .in15(d_ff_48_q), .out(OUT_D1), .sel(ADDRESS));
  Multiplexer #(.select(4), .enable("false")) multiplexer_4 (
    .in0(d_ff_49_q), .in1(d_ff_50_q), .in2(d_ff_51_q), .in3(d_ff_52_q), .in4(d_ff_53_q), .in5(d_ff_54_q),
    .in6(d_ff_55_q), .in7(d_ff_56_q), .in8(d_ff_57_q), .in9(d_ff_58_q), .in10(d_ff_59_q), .in11(d_ff_60_q),
    .in12(d_ff_61_q), .in13(d_ff_62_q), .in14(d_ff_63_q), .in15(d_ff_64_q), .out(OUT_D0), .sel(ADDRESS));
endmodule
