// Logisim project 1x2 DEMUX.circ as structural Verilog: 2 circuits, main circuit main
module main (
  input  A,
  input  Control,
  output Y1,
  output Y0
);

  wire not_1_out;

  not not_1 (not_1_out, Control);
  and and_1 (Y1, A, not_1_out);
  and and_2 (Y0, Control, A);

  // Notes on the sheet:
  //   1X2 DEMULTIPLEXER
endmodule

module demux2x1 (
  input  in_1,
  input  in_2,
  output out_3,
  output out_4
);

  main main_1 (.A(in_1), .Control(in_2), .Y1(out_3), .Y0(out_4));
endmodule
