// Logisim project 2 CROSS 4 DECODER WITH ACTIVE HIGH OUTPUT AND HS USING THE DECODER.circ as structural Verilog: 2 circuits, main circuit main
module main (
  input  A,
  input  B,
  output _00,
  output _01,
  output _10,
  output _11
);

  wire not_1_out, not_2_out;

  not not_1 (not_1_out, A);
  not not_2 (not_2_out, B);
  and and_1 (_00, not_1_out, not_2_out);
  and and_2 (_01, not_1_out, B);
  and and_3 (_10, A, not_2_out);
  and and_4 (_11, A, B);
endmodule

module HS (
  input  A,
  input  B,
  output DIFFERENCE,
  output BORROW
);

  wire main_1__00, main_1__01, main_1__10, main_1__11;

  main main_1 (.A(A), .B(B), ._00(main_1__00), ._01(main_1__01), ._10(main_1__10), ._11(main_1__11));
  and and_1 (BORROW, main_1__01, main_1__01);
  xor xor_1 (DIFFERENCE, main_1__01, main_1__10);

  // Notes on the sheet:
  //   0 LOW
  //   1 HIGH
endmodule
