// Logisim project 2 CROSS 4 DECODER WITH ACTIVE LOW OUTPUTS AND HA USING THE DECODER.circ as structural Verilog: 2 circuits, main circuit main
module main (
  input  A,
  input  B,
  output _00,
  output _01,
  output _10,
  output _11
);

  wire not_1_out, not_2_out;

  not not_1 (not_1_out, A);
  not not_2 (not_2_out, B);
  nand nand_1 (_00, not_2_out, not_1_out);
  nand nand_2 (_01, not_1_out, B);
  nand nand_3 (_10, A, not_2_out);
  nand nand_4 (_11, A, B);

  // Notes on the sheet:
  //   0 INDICATES "ON"
  //   1 INDICATES "OFF"
endmodule

module F (
  input  A,
  input  B,
  output SUM,
  output out_4
);

  wire main_1__00, main_1__01, main_1__10;

  main main_1 (.A(A), .B(B), ._00(main_1__00), ._01(main_1__01), ._10(main_1__10), ._11(out_4));
  nor nor_1 (SUM, ~main_1__01, ~main_1__10);  // NOR_Gate

  // Notes on the sheet:
  //   0 IS ON
  //   1 IS OFF
  //   (BUBBLE IS THE NOT GATE)
  //   HALF ADDER
  //   FOR OBTAINING ACTIVE LOW OUTPUT NOR GATE IS USED
  //   NOT GATE IS INSERTED IN HERE BECAUSE THE DECODER'S OUTPUT IS COMPLEMENT OF THE ORIGINAL OUTPUT
  //   CARRY
endmodule
