// Logisim project 3 BIT ASYNCHRONOUS COUNTER USING D FLIP FLOP.circ as structural Verilog: 1 circuit, main circuit main
module main (
  output Y2,
  output Y1,
  output Y0
);

  wire and_1_out, and_2_out, and_3_out, and_4_out, and_5_out, and_6_out, button_1_out, d_ff_1_qn, d_ff_2_qn,
       d_ff_3_qn, not_1_out, not_2_out, not_3_out, or_1_out, or_2_out, or_3_out;

  not not_1 (not_1_out, 1'b1);
  and and_1 (and_1_out, d_ff_1_qn, 1'b1);
  or or_1 (or_1_out, and_1_out, and_2_out);
  and and_2 (and_2_out, not_1_out, Y0);
  Button button_1 (.out(button_1_out));
  D_Flip_Flop #(.trigger("falling")) d_ff_1 (
    .clk(button_1_out), .D(or_1_out), .Q(Y0), .Qn(d_ff_1_qn));  // open: preset, en, reset
  not not_2 (not_2_out, 1'b1);
  and and_3 (and_3_out, d_ff_2_qn, 1'b1);
  and and_4 (and_4_out, not_2_out, Y1);
  or or_2 (or_2_out, and_3_out, and_4_out);
  D_Flip_Flop #(.trigger("falling")) d_ff_2 (
    .clk(Y0), .D(or_2_out), .Q(Y1), .Qn(d_ff_2_qn));  // open: preset, en, reset
  not not_3 (not_3_out, 1'b1);
  and and_5 (and_5_out, d_ff_3_qn, 1'b1);
  and and_6 (and_6_out, not_3_out, Y2);
  or or_3 (or_3_out, and_5_out, and_6_out);
  D_Flip_Flop #(.trigger("falling")) d_ff_3 (
    .clk(Y1), .D(or_3_out), .Q(Y2), .Qn(d_ff_3_qn));  // open: preset, en, reset

  // Notes on the sheet:
  //   T
endmodule
