// Logisim project 3 CROSS 8 DECODER ACTIVE HIGH OUTPUT AND FS USING THE DECODER.circ as structural Verilog: 2 circuits, main circuit main
module main (
  input  A,
  input  B,
  input  C,
  output _000,
  output _001,
  output _010,
  output _011,
  output _100,
  output _101,
  output _110,
  output _111
);

  wire not_1_out, not_2_out, not_3_out;

  not not_1 (not_1_out, A);
  not not_2 (not_2_out, C);
  not not_3 (not_3_out, B);
  and and_1 (_000, not_1_out, not_3_out, not_2_out);
  and and_2 (_001, not_1_out, not_3_out, C);
  and and_3 (_010, not_1_out, B, not_2_out);
  and and_4 (_011, not_1_out, B, C);
  and and_5 (_100, A, not_3_out, not_2_out);
  and and_6 (_101, A, not_3_out, C);
  and and_7 (_110, A, B, not_2_out);
  and and_8 (_111, A, B, C);
endmodule

module FS (
  input  A,
  input  B,
  input  C,
  output DIFFERENCE,
  output BORROW
);

  wire main_1__000, main_1__001, main_1__010, main_1__011, main_1__100, main_1__101, main_1__110, main_1__111;

  main main_1 (
    .A(A), .B(B), .C(C), ._000(main_1__000), ._001(main_1__001), ._010(main_1__010), ._011(main_1__011),
    ._100(main_1__100), ._101(main_1__101), ._110(main_1__110), ._111(main_1__111));
  or or_1 (BORROW, main_1__001, main_1__010, main_1__011, main_1__111);
  or or_2 (DIFFERENCE, main_1__001, main_1__010, main_1__100, main_1__111);
endmodule
