// Logisim project 3 CROSS 8 DECODER USING 2 CROSS 4 DECODER.circ as structural Verilog: 1 circuit, main circuit main
module main (
  input  A,
  input  [1:0] B1_B0,
  output Y7,
  output Y6,
  output Y5,
  output Y4,
  output Y3,
  output Y2,
  output Y1,
  output Y0
);

  wire not_1_out;

  Decoder #(.select(2)) decoder_1 (.out0(Y7), .out1(Y6), .out2(Y5), .out3(Y4), .sel(B1_B0), .en(not_1_out));
  not not_1 (not_1_out, A);
  Decoder #(.select(2)) decoder_2 (.out0(Y3), .out1(Y2), .out2(Y1), .out3(Y0), .sel(B1_B0), .en(A));
endmodule
