// Logisim project 3 CROSS 8 DECODER WITH ACTIVE LOW OUTPUTS AND FA USING THE DECODER.circ as structural Verilog: 2 circuits, main circuit main
module main (
  input  A,
  input  B,
  input  C,
  output _000,
  output _001,
  output _010,
  output _011,
  output _100,
  output _101,
  output _110,
  output _111
);

  wire not_1_out, not_2_out, not_3_out;

  not not_1 (not_1_out, B);
  not not_2 (not_2_out, A);
  not not_3 (not_3_out, C);
  nand nand_1 (_000, not_2_out, not_1_out, not_3_out);
  nand nand_2 (_001, not_2_out, not_1_out, C);
  nand nand_3 (_010, not_2_out, B, not_3_out);
  nand nand_4 (_011, not_2_out, B, C);
  nand nand_5 (_100, A, not_1_out, not_3_out);
  nand nand_6 (_101, A, not_1_out, C);
  nand nand_7 (_110, A, B, not_3_out);
  nand nand_8 (_111, A, B, C);
endmodule

module FA (
  input  A,
  input  B,
  input  C,
  output SUM,
  output CARRY
);

  wire main_1__000, main_1__001, main_1__010, main_1__011, main_1__100, main_1__101, main_1__110, main_1__111;

  main main_1 (
    .A(A), .B(B), .C(C), ._000(main_1__000), ._001(main_1__001), ._010(main_1__010), ._011(main_1__011),
    ._100(main_1__100), ._101(main_1__101), ._110(main_1__110), ._111(main_1__111));
  nor nor_1 (SUM, ~main_1__001, ~main_1__010, ~main_1__100, ~main_1__111);  // NOR_Gate
  nor nor_2 (CARRY, ~main_1__011, ~main_1__101, ~main_1__110, ~main_1__111);  // NOR_Gate
endmodule
