// Logisim project 5 BIT PARALLEL ADDER CUM SUBTRACTOR.circ as structural Verilog: 2 circuits, main circuit main
module main (
  input  in_1,
  input  in_2,
  input  in_3,
  output out_4,
  output out_5
);

  wire and_1_out, and_2_out, xor_1_out;

  xor xor_1 (xor_1_out, in_1, in_2);
  and and_1 (and_1_out, xor_1_out, in_3);
  and and_2 (and_2_out, in_1, in_2);
  xor xor_2 (out_4, xor_1_out, in_3);
  or or_1 (out_5, and_1_out, and_2_out);
endmodule

module _5_BIT_ADDER_CUM_SUBTRACTOR (
  input  X,
  input  B4,
  input  B3,
  input  B2,
  input  B1,
  input  B0,
  input  A4,
  input  A3,
  input  A2,
  input  A1,
  input  A0,
  output out_12,
  output out_13,
  output out_14,
  output out_15,
  output out_16,
  output out_17
);

  wire main_2_out_5, main_3_out_5, main_4_out_5, main_5_out_5, xor_1_out, xor_2_out, xor_3_out, xor_4_out,
       xor_5_out;

  xor xor_1 (xor_1_out, B4, X);
  main main_1 (.in_1(main_2_out_5), .in_2(xor_1_out), .in_3(A4), .out_4(out_13), .out_5(out_12));
  xor xor_2 (xor_2_out, B3, X);
  main main_2 (.in_1(main_3_out_5), .in_2(xor_2_out), .in_3(A3), .out_4(out_14), .out_5(main_2_out_5));
  xor xor_3 (xor_3_out, B2, X);
  main main_3 (.in_1(main_4_out_5), .in_2(xor_3_out), .in_3(A2), .out_4(out_15), .out_5(main_3_out_5));
  xor xor_4 (xor_4_out, B1, X);
  main main_4 (.in_1(main_5_out_5), .in_2(xor_4_out), .in_3(A1), .out_4(out_16), .out_5(main_4_out_5));
  xor xor_5 (xor_5_out, B0, X);
  main main_5 (.in_1(X), .in_2(xor_5_out), .in_3(A0), .out_4(out_17), .out_5(main_5_out_5));

  // Notes on the sheet:
  //   IF X = 0, 5 BIT PARALLEL ADDER
  //   IF X=1, 5 BIT PARALLEL SUBTRACTOR
endmodule
