// Logisim project ACTIVE HIGH ENABLE INPUT DECODER AND HS.circ as structural Verilog: 2 circuits, main circuit main
module main (
  input  in_1,
  input  in_2,
  output out_3,
  output out_4,
  output out_5,
  output out_6
);

  wire not_1_out, not_2_out;

  not not_1 (not_1_out, in_1);
  not not_2 (not_2_out, in_2);
  and and_1 (out_3, not_1_out, not_2_out);
  and and_2 (out_4, not_1_out, in_2);
  and and_3 (out_5, in_1, not_2_out);
  and and_4 (out_6, in_1, in_2);
endmodule

module HS_USING_2_4_DECODER (
  input  A,
  input  B,
  output SUM,
  output CARRY
);

  wire main_1_out_5;

  main main_1 (.in_1(A), .in_2(B), .out_4(CARRY), .out_5(main_1_out_5));  // open: out_3, out_6
  or or_1 (SUM, CARRY, main_1_out_5);
endmodule
