// Logisim project BARREL SHIFTER 4 BIT.circ as structural Verilog: 1 circuit, main circuit main
module main (
  input  A0,
  input  A1,
  input  A2,
  input  A3,
  input  in_5,
  input  in_6,
  output Y0,
  output Y1,
  output Y2,
  output Y3
);

  wire multiplexer_1_out, multiplexer_2_out, multiplexer_3_out, multiplexer_4_out;

  Multiplexer #(.enable("false")) multiplexer_1 (.in0(A0), .in1(A2), .out(multiplexer_1_out), .sel(in_5));
  Multiplexer #(.enable("false")) multiplexer_2 (.in0(A1), .in1(A3), .out(multiplexer_2_out), .sel(in_5));
  Multiplexer #(.enable("false")) multiplexer_3 (.in0(A2), .in1(A0), .out(multiplexer_3_out), .sel(in_5));
  Multiplexer #(.enable("false")) multiplexer_4 (.in0(A3), .in1(A1), .out(multiplexer_4_out), .sel(in_5));
  Multiplexer #(.enable("false")) multiplexer_5 (
    .in0(multiplexer_1_out), .in1(multiplexer_4_out), .out(Y0), .sel(in_6));
  Multiplexer #(.enable("false")) multiplexer_6 (
    .in0(multiplexer_2_out), .in1(multiplexer_1_out), .out(Y1), .sel(in_6));
  Multiplexer #(.enable("false")) multiplexer_7 (
    .in0(multiplexer_3_out), .in1(multiplexer_2_out), .out(Y2), .sel(in_6));
  Multiplexer #(.enable("false")) multiplexer_8 (
    .in0(multiplexer_4_out), .in1(multiplexer_3_out), .out(Y3), .sel(in_6));
endmodule
