// Logisim project BARREL_SHIFTER_8-BIT.circ as structural Verilog: 1 circuit, main circuit main
module main (
  input  A0,
  input  A1,
  input  A2,
  input  A3,
  input  A4,
  input  A5,
  input  A6,
  input  A7,
  input  in_9,
  input  in_10,
  input  in_11,
  output Y0,
  output Y1,
  output Y2,
  output Y3,
  output Y4,
  output Y5,
  output Y6,
  output Y7
);

  wire multiplexer_1_out, multiplexer_2_out, multiplexer_3_out, multiplexer_4_out, multiplexer_5_out,
       multiplexer_6_out, multiplexer_7_out, multiplexer_8_out, multiplexer_9_out, multiplexer_10_out,
       multiplexer_11_out, multiplexer_12_out, multiplexer_13_out, multiplexer_14_out, multiplexer_15_out,
       multiplexer_16_out;

  Multiplexer #(.enable("false")) multiplexer_1 (.in0(A0), .in1(A5), .out(multiplexer_1_out), .sel(in_9));
  Multiplexer #(.enable("false")) multiplexer_2 (.in0(A1), .in1(A6), .out(multiplexer_2_out), .sel(in_9));
  Multiplexer #(.enable("false")) multiplexer_3 (.in0(A2), .in1(A7), .out(multiplexer_3_out), .sel(in_9));
  Multiplexer #(.enable("false")) multiplexer_4 (.in0(A3), .in1(A0), .out(multiplexer_4_out), .sel(in_9));
  Multiplexer #(.enable("false")) multiplexer_5 (.in0(A4), .in1(A1), .out(multiplexer_5_out), .sel(in_9));
  Multiplexer #(.enable("false")) multiplexer_6 (.in0(A5), .in1(A2), .out(multiplexer_6_out), .sel(in_9));
  Multiplexer #(.enable("false")) multiplexer_7 (.in0(A6), .in1(A3), .out(multiplexer_7_out), .sel(in_9));
  Multiplexer #(.enable("false")) multiplexer_8 (.in0(A7), .in1(A4), .out(multiplexer_8_out), .sel(in_9));
  Multiplexer #(.enable("false")) multiplexer_9 (
    .in0(multiplexer_1_out), .in1(multiplexer_7_out), .out(multiplexer_9_out), .sel(in_10));
  Multiplexer #(.enable("false")) multiplexer_10 (
    .in0(multiplexer_2_out), .in1(multiplexer_8_out), .out(multiplexer_10_out), .sel(in_10));
  Multiplexer #(.enable("false")) multiplexer_11 (
    .in0(multiplexer_3_out), .in1(multiplexer_1_out), .out(multiplexer_11_out), .sel(in_10));
  Multiplexer #(.enable("false")) multiplexer_12 (
    .in0(multiplexer_4_out), .in1(multiplexer_2_out), .out(multiplexer_12_out), .sel(in_10));
  Multiplexer #(.enable("false")) multiplexer_13 (
    .in0(multiplexer_5_out), .in1(multiplexer_3_out), .out(multiplexer_13_out), .sel(in_10));
  Multiplexer #(.enable("false")) multiplexer_14 (
    .in0(multiplexer_6_out), .in1(multiplexer_4_out), .out(multiplexer_14_out), .sel(in_10));
  Multiplexer #(.enable("false")) multiplexer_15 (
    .in0(multiplexer_7_out), .in1(multiplexer_5_out), .out(multiplexer_15_out), .sel(in_10));
  Multiplexer #(.enable("false")) multiplexer_16 (
    .in0(multiplexer_8_out), .in1(multiplexer_6_out), .out(multiplexer_16_out), .sel(in_10));
  Multiplexer #(.enable("false")) multiplexer_17 (
    .in0(multiplexer_9_out), .in1(multiplexer_16_out), .out(Y0), .sel(in_11));
  Multiplexer #(.enable("false")) multiplexer_18 (
    .in0(multiplexer_10_out), .in1(multiplexer_9_out), .out(Y1), .sel(in_11));
  Multiplexer #(.enable("false")) multiplexer_19 (
    .in0(multiplexer_11_out), .in1(multiplexer_10_out), .out(Y2), .sel(in_11));
  Multiplexer #(.enable("false")) multiplexer_20 (
    .in0(multiplexer_12_out), .in1(multiplexer_11_out), .out(Y3), .sel(in_11));
  Multiplexer #(.enable("false")) multiplexer_21 (
    .in0(multiplexer_13_out), .in1(multiplexer_12_out), .out(Y4), .sel(in_11));
  Multiplexer #(.enable("false")) multiplexer_22 (
    .in0(multiplexer_14_out), .in1(multiplexer_13_out), .out(Y5), .sel(in_11));
  Multiplexer #(.enable("false")) multiplexer_23 (
    .in0(multiplexer_15_out), .in1(multiplexer_14_out), .out(Y6), .sel(in_11));
  Multiplexer #(.enable("false")) multiplexer_24 (
    .in0(multiplexer_16_out), .in1(multiplexer_15_out), .out(Y7), .sel(in_11));
endmodule
