// Logisim project CARRY SAVE ADDER.circ as structural Verilog: 1 circuit, main circuit main
module main (
  input  A0,
  input  in_2,
  input  in_3,
  input  B0,
  input  A1,
  input  in_6,
  input  B1,
  input  A2,
  input  in_9,
  input  B2,
  input  A3,
  input  in_12,
  input  B3,
  input  in_14,
  output S0,
  output S1,
  output S2,
  output S3,
  output S4,
  output Cout
);

  wire adder_1_cout, adder_2_cout, adder_2_out, adder_3_cout, adder_3_out, adder_4_cout, adder_4_out,
       adder_5_cout, adder_6_cout, adder_7_cout;

  Adder #(.width(1)) adder_1 (.a(A0), .b(B0), .out(S0), .cin(in_2), .cout(adder_1_cout));
  Adder #(.width(1)) adder_2 (.a(A1), .b(B1), .out(adder_2_out), .cin(in_6), .cout(adder_2_cout));
  Adder #(.width(1)) adder_3 (.a(A2), .b(B2), .out(adder_3_out), .cin(in_9), .cout(adder_3_cout));
  Adder #(.width(1)) adder_4 (.a(A3), .b(B3), .out(adder_4_out), .cin(in_12), .cout(adder_4_cout));
  Adder #(.width(1)) adder_5 (.a(adder_1_cout), .b(adder_2_out), .out(S1), .cin(in_3), .cout(adder_5_cout));
  Adder #(.width(1)) adder_6 (.a(adder_2_cout), .b(adder_3_out), .out(S2), .cin(adder_5_cout), .cout(adder_6_cout));
  Adder #(.width(1)) adder_7 (.a(adder_3_cout), .b(adder_4_out), .out(S3), .cin(adder_6_cout), .cout(adder_7_cout));
  Adder #(.width(1)) adder_8 (.a(adder_4_cout), .b(in_14), .out(S4), .cin(adder_7_cout), .cout(Cout));
endmodule
