// Logisim project DECADE SYNCHRONOUS UP COUNTER USING T FLIP-FLOPS.circ as structural Verilog: 1 circuit, main circuit main
module main (
  input  in_1,
  output out_2,
  output out_3,
  output out_4,
  output out_5
);

  wire and_1_out, and_2_out, and_3_out, and_4_out, and_5_out, and_6_out, and_7_out, and_8_out, clock_1_out,
       or_1_out, or_2_out, or_3_out, t_ff_1_qn, t_ff_2_qn, t_ff_3_qn, t_ff_4_qn;

  Clock clock_1 (.out(clock_1_out));
  or or_1 (or_1_out, and_1_out, and_2_out);
  and and_1 (and_1_out, t_ff_1_qn, out_3, out_4, out_5);
  and and_2 (and_2_out, out_2, t_ff_2_qn, out_4, t_ff_4_qn);
  and and_3 (and_3_out, out_2, t_ff_2_qn, t_ff_3_qn, out_5);
  and and_4 (and_4_out, out_2, t_ff_2_qn, t_ff_4_qn, out_4);
  T_Flip_Flop t_ff_1 (.clk(clock_1_out), .T(or_1_out), .Q(out_2), .Qn(t_ff_1_qn), .reset(in_1));  // open: preset, en
  and and_5 (and_5_out, t_ff_1_qn, out_4, out_5);
  and and_6 (and_6_out, t_ff_1_qn, out_5);
  T_Flip_Flop t_ff_2 (.clk(clock_1_out), .T(and_5_out), .Q(out_3), .Qn(t_ff_2_qn), .reset(in_1));  // open: preset, en
  or or_2 (or_2_out, and_3_out, and_4_out, and_6_out);
  T_Flip_Flop t_ff_3 (.clk(clock_1_out), .T(or_2_out), .Q(out_4), .Qn(t_ff_3_qn), .reset(in_1));  // open: preset, en
  or or_3 (or_3_out, t_ff_1_qn, out_3, and_7_out, and_8_out);
  and and_7 (and_7_out, out_2, t_ff_3_qn);
  T_Flip_Flop t_ff_4 (.clk(clock_1_out), .T(or_3_out), .Q(out_5), .Qn(t_ff_4_qn), .reset(in_1));  // open: preset, en
  and and_8 (and_8_out, out_2, out_5);
endmodule
