// Logisim project FA AND 4 BIT PARALLEL ADDER USING FA.circ as structural Verilog: 2 circuits, main circuit main
module main (
  input  in_1,
  input  in_2,
  input  in_3,
  output out_4,
  output out_5
);

  wire and_1_out, and_2_out, xor_1_out;

  xor xor_1 (xor_1_out, in_1, in_2);
  and and_1 (and_1_out, in_2, in_1);
  xor xor_2 (out_4, xor_1_out, in_3);
  and and_2 (and_2_out, xor_1_out, in_3);
  or or_1 (out_5, and_2_out, and_1_out);

  // Notes on the sheet:
  //   FULL ADDER
endmodule

module _4_BIT_PARALLEL_ADDER (
  input  in_1,
  input  in_2,
  input  in_3,
  input  in_4,
  input  in_5,
  input  in_6,
  input  in_7,
  input  in_8,
  input  in_9,
  output out_10,
  output out_11,
  output out_12,
  output out_13,
  output out_14
);

  wire main_2_out_5, main_3_out_5, main_4_out_5;

  main main_1 (.in_1(in_6), .in_2(in_2), .in_3(main_2_out_5), .out_4(out_11), .out_5(out_10));
  main main_2 (.in_1(in_7), .in_2(in_3), .in_3(main_3_out_5), .out_4(out_12), .out_5(main_2_out_5));
  main main_3 (.in_1(in_8), .in_2(in_4), .in_3(main_4_out_5), .out_4(out_13), .out_5(main_3_out_5));
  main main_4 (.in_1(in_9), .in_2(in_5), .in_3(in_1), .out_4(out_14), .out_5(main_4_out_5));
endmodule
