// Logisim project FA AND FS USING HA AND HS RESPECTIVELY.circ as structural Verilog: 4 circuits, main circuit main
module main (
  input  A,
  input  B,
  output SUM__S,
  output CARRY__C
);

  xor xor_1 (SUM__S, A, B);
  and and_1 (CARRY__C, A, B);

  // Notes on the sheet:
  //   HALF ADDER
endmodule

module FA_USING_HA (
  input  A,
  input  B,
  input  C,
  input  A_2,
  input  B_2,
  input  C_2,
  output SUM__S,
  output CARRY__C,
  output SUM__S_2,
  output CARRY__C_2
);

  wire and_1_out, and_2_out, main_1_carry__c, main_1_sum__s, main_2_carry__c, xor_1_out;

  xor xor_1 (xor_1_out, A, B);
  and and_1 (and_1_out, A, B);
  main main_1 (.A(A_2), .B(B_2), .SUM__S(main_1_sum__s), .CARRY__C(main_1_carry__c));
  xor xor_2 (SUM__S, xor_1_out, C);
  and and_2 (and_2_out, xor_1_out, C);
  main main_2 (.A(main_1_sum__s), .B(C_2), .SUM__S(SUM__S_2), .CARRY__C(main_2_carry__c));
  or or_1 (CARRY__C_2, main_2_carry__c, main_1_carry__c);
  or or_2 (CARRY__C, and_1_out, and_2_out);

  // Notes on the sheet:
  //   FULL ADDER
  //   FULL ADDER USING HALF ADDER
endmodule

module HS (
  input  A,
  input  B,
  output DIFFERENCE__D,
  output BORROW__B
);

  wire not_1_out;

  not not_1 (not_1_out, A);
  xor xor_1 (DIFFERENCE__D, A, B);
  and and_1 (BORROW__B, not_1_out, B);

  // Notes on the sheet:
  //   HALF SUBTRACTOR
endmodule

module FS_USING_HS (
  input  A,
  input  B,
  input  C,
  output DIFFERENCE__D,
  output BORROW__B
);

  wire hs_1_borrow__b, hs_1_difference__d, hs_2_borrow__b;

  HS hs_1 (.A(A), .B(B), .DIFFERENCE__D(hs_1_difference__d), .BORROW__B(hs_1_borrow__b));
  HS hs_2 (.A(hs_1_difference__d), .B(C), .DIFFERENCE__D(DIFFERENCE__D), .BORROW__B(hs_2_borrow__b));
  or or_1 (BORROW__B, hs_2_borrow__b, hs_1_borrow__b);

  // Notes on the sheet:
  //   FULL SUBTRACTOR USING HALF SUBTRACTOR
endmodule
