// Logisim project FA USING 8 CROSS 1 MUX.circ as structural Verilog: 1 circuit, main circuit main
module main (
  input  _0,
  input  _0_2,
  input  S___1,
  input  Cout___1,
  input  [2:0] A_B_Cin,
  output Y,
  output Y_2
);

  Multiplexer #(.select(3)) multiplexer_1 (
    .in0(_0), .in1(S___1), .in2(S___1), .in3(_0), .in4(S___1), .in5(_0), .in6(_0), .in7(S___1), .out(Y),
    .sel(A_B_Cin));  // open: en
  Multiplexer #(.select(3)) multiplexer_2 (
    .in0(_0_2), .in1(_0_2), .in2(_0_2), .in3(Cout___1), .in4(_0_2), .in5(Cout___1), .in6(Cout___1),
    .in7(Cout___1), .out(Y_2), .sel(A_B_Cin));  // open: en

  // Notes on the sheet:
  //   MUX FOR SUM
  //   MUX FOR CARRY OUT
endmodule
