// Logisim project FA USING NAND - NAND LOGIC.circ as structural Verilog: 1 circuit, main circuit main
module main (
  input  in_1,
  input  in_2,
  input  in_3,
  input  in_4,
  input  in_5,
  input  in_6,
  output out_7,
  output out_8,
  output out_9,
  output out_10
);

  wire and_1_out, and_2_out, nand_1_out, nand_2_out, nand_3_out, nand_4_out, nand_5_out, nand_6_out,
       nand_7_out, xor_1_out;

  nand nand_1 (nand_1_out, in_4, in_5);
  xor xor_1 (xor_1_out, in_1, in_2);
  nand nand_2 (nand_2_out, in_4, nand_1_out);
  nand nand_3 (nand_3_out, nand_1_out, in_5);
  xor xor_2 (out_7, xor_1_out, in_3);
  and and_1 (and_1_out, xor_1_out, in_3);
  and and_2 (and_2_out, in_1, in_2);
  nand nand_4 (nand_4_out, nand_2_out, nand_3_out);
  or or_1 (out_8, and_1_out, and_2_out);
  nand nand_5 (nand_5_out, nand_4_out, in_6);
  nand nand_6 (nand_6_out, nand_4_out, nand_5_out);
  nand nand_7 (nand_7_out, nand_5_out, in_6);
  nand nand_8 (out_10, nand_5_out, nand_1_out);
  nand nand_9 (out_9, nand_6_out, nand_7_out);

  // Notes on the sheet:
  //   FULL ADDER
  //   FULL ADDER USING NAND - NAND LOGIC
endmodule
