// Logisim project HA , HS USING NAND GATES.circ as structural Verilog: 1 circuit, main circuit main
module main (
  input  in_1,
  input  in_2,
  input  in_3,
  input  in_4,
  output out_5,
  output out_6,
  output out_7,
  output out_8
);

  wire nand_1_out, nand_2_out, nand_3_out, nand_4_out, nand_5_out, nand_6_out, nand_7_out, nand_8_out,
       nand_10_out, nand_11_out;

  nand nand_1 (nand_1_out, in_1, in_1);
  nand nand_2 (nand_2_out, in_2, in_2);
  nand nand_3 (nand_3_out, in_1, in_2);
  nand nand_4 (nand_4_out, in_3, in_3);
  nand nand_5 (nand_5_out, in_4, in_4);
  nand nand_6 (nand_6_out, nand_4_out, in_4);
  nand nand_7 (nand_7_out, in_2, nand_1_out);
  nand nand_8 (nand_8_out, in_1, nand_2_out);
  nand nand_9 (out_6, nand_3_out, nand_3_out);
  nand nand_10 (nand_10_out, in_4, nand_4_out);
  nand nand_11 (nand_11_out, in_3, nand_5_out);
  nand nand_12 (out_8, nand_6_out, nand_6_out);
  nand nand_13 (out_5, nand_7_out, nand_8_out);
  nand nand_14 (out_7, nand_10_out, nand_11_out);

  // Notes on the sheet:
  //   HALF ADDER USING NAND GATES
  //   HALF SUBTRACTOR USING NAND GATES
endmodule
