// Logisim project HA AND FA USING HA.circ as structural Verilog: 2 circuits, main circuit main
module main (
  input  in_1,
  input  in_2,
  output out_3,
  output out_4
);

  xor xor_1 (out_3, in_1, in_2);
  and and_1 (out_4, in_2, in_1);

  // Notes on the sheet:
  //   HALF ADDER USING BASIC GATES
endmodule

module FA_USING_HA (
  input  in_1,
  input  in_2,
  input  in_3,
  output out_4,
  output out_5
);

  wire main_1_out_3, main_1_out_4, main_2_out_4;

  main main_1 (.in_1(in_2), .in_2(in_3), .out_3(main_1_out_3), .out_4(main_1_out_4));
  main main_2 (.in_1(in_1), .in_2(main_1_out_3), .out_3(out_4), .out_4(main_2_out_4));
  or or_1 (out_5, main_2_out_4, main_1_out_4);
endmodule
