// Logisim project Implement the function F(A,B,C,D)=∑(1,2,5,6,9,11,13,15) using decoder.circ as structural Verilog: 1 circuit, main circuit main
module main (
  input  [3:0] in_1,
  output out_2
);

  wire decoder_1_out1, decoder_1_out2, decoder_1_out5, decoder_1_out6, decoder_1_out9, decoder_1_out11,
       decoder_1_out13, decoder_1_out15;

  Decoder #(.select(4)) decoder_1 (
    .out1(decoder_1_out1), .out2(decoder_1_out2), .out5(decoder_1_out5), .out6(decoder_1_out6),
    .out9(decoder_1_out9), .out11(decoder_1_out11), .out13(decoder_1_out13), .out15(decoder_1_out15),
    .sel(in_1));  // open: out0, out3, out4, out7, out8, out10, out12, out14, en
  or or_1 (out_2, decoder_1_out1, decoder_1_out2, decoder_1_out5, decoder_1_out6, decoder_1_out9, decoder_1_out11, decoder_1_out13, decoder_1_out15);
endmodule
