// Logisim project MOD 5 RIPPLE COUNTER.circ as structural Verilog: 1 circuit, main circuit main
module main (
  output QC,
  output QB,
  output QA
);

  wire and_1_out, clock_1_out;

  Clock clock_1 (.out(clock_1_out));
  J_K_Flip_Flop #(.trigger("falling")) j_k_ff_1 (
    .J(1'b1), .clk(clock_1_out), .K(1'b1), .Q(QA), .reset(and_1_out));  // open: Qn, preset, en
  J_K_Flip_Flop #(.trigger("falling")) j_k_ff_2 (
    .J(1'b1), .clk(QA), .K(1'b1), .Q(QB), .reset(and_1_out));  // open: Qn, preset, en
  J_K_Flip_Flop #(.trigger("falling")) j_k_ff_3 (
    .J(1'b1), .clk(QB), .K(1'b1), .Q(QC), .reset(and_1_out));  // open: Qn, preset, en
  and and_1 (and_1_out, QA, QC);

  // Notes on the sheet:
  //   J AND K OF ALL F.Fs CONNECTED TO ACTIVE HIGH
  //   CLOCK
  //   CLR
  //   CLR
  //   CLR
  //   (MSB)
  //   (LSB)
endmodule
