// Logisim project MOD-10 SYNCHRONOUS COUNTER USING D FLIP FLOPS.circ as structural Verilog: 1 circuit, main circuit main
module main (
  input  in_1,
  output out_2,
  output out_3,
  output out_4,
  output out_5
);

  wire and_1_out, and_2_out, and_3_out, and_4_out, and_5_out, and_6_out, and_7_out, and_8_out, and_9_out,
       and_10_out, and_11_out, and_12_out, and_13_out, and_14_out, and_15_out, button_1_out, d_ff_1_qn,
       d_ff_2_qn, d_ff_3_qn, d_ff_4_qn, not_1_out, not_2_out, not_3_out, not_4_out, or_1_out, or_2_out,
       or_3_out, or_4_out, or_5_out, or_6_out, or_7_out;

  Button button_1 (.out(button_1_out));
  not not_1 (not_1_out, or_1_out);
  or or_1 (or_1_out, and_3_out, and_4_out);
  and and_1 (and_1_out, d_ff_1_qn, or_1_out);
  and and_2 (and_2_out, not_1_out, out_2);
  and and_3 (and_3_out, d_ff_4_qn, out_4, d_ff_2_qn, out_2);
  and and_4 (and_4_out, out_5, out_4, out_3, d_ff_1_qn);
  or or_2 (or_2_out, and_1_out, and_2_out);
  D_Flip_Flop d_ff_1 (.clk(button_1_out), .D(or_2_out), .Q(out_2), .Qn(d_ff_1_qn), .reset(in_1));  // open: preset, en
  and and_5 (and_5_out, d_ff_2_qn, and_7_out);
  not not_2 (not_2_out, and_7_out);
  and and_6 (and_6_out, not_2_out, out_3);
  and and_7 (and_7_out, out_5, out_4, d_ff_1_qn);
  or or_3 (or_3_out, and_5_out, and_6_out);
  D_Flip_Flop d_ff_2 (.clk(button_1_out), .D(or_3_out), .Q(out_3), .Qn(d_ff_2_qn), .reset(in_1));  // open: preset, en
  not not_3 (not_3_out, or_4_out);
  or or_4 (or_4_out, and_10_out, and_11_out, and_12_out);
  and and_8 (and_8_out, d_ff_3_qn, or_4_out);
  and and_9 (and_9_out, not_3_out, out_4);
  and and_10 (and_10_out, out_5, d_ff_1_qn);
  and and_11 (and_11_out, out_5, d_ff_3_qn, d_ff_2_qn, out_2);
  and and_12 (and_12_out, d_ff_4_qn, out_4, d_ff_2_qn, out_2);
  or or_5 (or_5_out, and_8_out, and_9_out);
  D_Flip_Flop d_ff_3 (.clk(button_1_out), .D(or_5_out), .Q(out_4), .Qn(d_ff_3_qn), .reset(in_1));  // open: preset, en
  or or_6 (or_6_out, d_ff_1_qn, and_15_out);
  not not_4 (not_4_out, or_6_out);
  and and_13 (and_13_out, d_ff_4_qn, or_6_out);
  and and_14 (and_14_out, not_4_out, out_5);
  and and_15 (and_15_out, d_ff_2_qn, d_ff_3_qn);
  or or_7 (or_7_out, and_13_out, and_14_out);
  D_Flip_Flop d_ff_4 (.clk(button_1_out), .D(or_7_out), .Q(out_5), .Qn(d_ff_4_qn), .reset(in_1));  // open: preset, en
endmodule
