// Logisim project MOD-16 RIPPLE COUNTER USING D FLIP FLOP.circ as structural Verilog
module main (
  input  in_1,
  output out_2,
  output out_3,
  output out_4,
  output out_5
);

  wire and_1_out, and_2_out, and_3_out, and_4_out, and_5_out, and_6_out, and_7_out, and_8_out, button_1_out,
       d_ff_1_qn, d_ff_2_qn, d_ff_3_qn, d_ff_4_qn, not_1_out, not_2_out, not_3_out, not_4_out, or_1_out,
       or_2_out, or_3_out, or_4_out;

  and and_1 (and_1_out, d_ff_1_qn, 1'b1);
  not not_1 (not_1_out, 1'b1);
  and and_2 (and_2_out, not_1_out, out_5);
  or or_1 (or_1_out, and_1_out, and_2_out);
  D_Flip_Flop #(.trigger("falling")) d_ff_1 (
    .clk(button_1_out), .D(or_1_out), .Q(out_5), .Qn(d_ff_1_qn), .reset(in_1));  // open: preset, en
  Button button_1 (.out(button_1_out));
  and and_3 (and_3_out, d_ff_2_qn, 1'b1);
  not not_2 (not_2_out, 1'b1);
  and and_4 (and_4_out, not_2_out, out_4);
  or or_2 (or_2_out, and_3_out, and_4_out);
  D_Flip_Flop #(.trigger("falling")) d_ff_2 (
    .clk(out_5), .D(or_2_out), .Q(out_4), .Qn(d_ff_2_qn), .reset(in_1));  // open: preset, en
  not not_3 (not_3_out, 1'b1);
  and and_5 (and_5_out, d_ff_3_qn, 1'b1);
  and and_6 (and_6_out, not_3_out, out_3);
  or or_3 (or_3_out, and_5_out, and_6_out);
  D_Flip_Flop #(.trigger("falling")) d_ff_3 (
    .clk(out_4), .D(or_3_out), .Q(out_3), .Qn(d_ff_3_qn), .reset(in_1));  // open: preset, en
  and and_7 (and_7_out, d_ff_4_qn, 1'b1);
  not not_4 (not_4_out, 1'b1);
  and and_8 (and_8_out, not_4_out, out_2);
  or or_4 (or_4_out, and_7_out, and_8_out);
  D_Flip_Flop #(.trigger("falling")) d_ff_4 (
    .clk(out_3), .D(or_4_out), .Q(out_2), .Qn(d_ff_4_qn), .reset(in_1));  // open: preset, en
endmodule
