// Logisim project MOD-16 SYNCHRONOUS COUNTER USING T FLIP-FLOP.circ as structural Verilog: 1 circuit, main circuit main
module main (
  input  in_1,
  input  in_2,
  output out_3,
  output out_4,
  output out_5,
  output out_6
);

  wire and_1_out, and_2_out, clock_1_out, t_ff_4_qn;

  Clock clock_1 (.out(clock_1_out));
  and and_1 (and_1_out, t_ff_4_qn, out_5, out_4);
  T_Flip_Flop t_ff_1 (.clk(clock_1_out), .T(and_1_out), .Q(out_3), .reset(in_2));  // open: Qn, preset, en
  and and_2 (and_2_out, t_ff_4_qn, out_5);
  T_Flip_Flop t_ff_2 (.clk(clock_1_out), .T(and_2_out), .Q(out_4), .reset(in_2));  // open: Qn, preset, en
  T_Flip_Flop t_ff_3 (.clk(clock_1_out), .T(t_ff_4_qn), .Q(out_5), .reset(in_2));  // open: Qn, preset, en
  T_Flip_Flop t_ff_4 (.clk(clock_1_out), .T(in_1), .Q(out_6), .Qn(t_ff_4_qn), .reset(in_2));  // open: preset, en
endmodule
