// Logisim project Prime Number.circ as structural Verilog: 1 circuit, main circuit main
module main (
  input  _5th_digit,
  input  _4th_digit,
  input  _3rd_digit,
  input  _2nd_digit,
  input  _1st_digit,
  output out_6
);

  wire and_1_out, and_2_out, and_3_out, and_4_out, and_5_out, and_6_out, or_1_out, or_2_out;

  and and_1 (and_1_out, ~_5th_digit, _3rd_digit, ~_2nd_digit, _1st_digit);  // AND_Gate
  and and_2 (and_2_out, ~_4th_digit, _2nd_digit, _1st_digit);  // AND_Gate
  and and_3 (and_3_out, ~_5th_digit, ~_3rd_digit, _2nd_digit, _1st_digit);  // AND_Gate
  and and_4 (and_4_out, ~_5th_digit, ~_4th_digit, ~_3rd_digit, _2nd_digit);  // AND_Gate
  and and_5 (and_5_out, _5th_digit, ~_4th_digit, ~_3rd_digit, _1st_digit);  // AND_Gate
  and and_6 (and_6_out, _5th_digit, _4th_digit, _3rd_digit, _1st_digit);
  or or_1 (or_1_out, and_1_out, and_2_out, and_3_out);
  or or_2 (or_2_out, and_4_out, and_5_out, and_6_out);
  or or_3 (out_6, or_1_out, or_2_out);

  // Notes on the sheet:
  //   If Prime, Output = 1. If not, Output = 0
endmodule
