// Logisim project mod 10 synchronous counter using t flip flops.circ as structural Verilog: 2 circuits, main circuit main
module main (
  input  in_1,
  output out_2,
  output out_3,
  output out_4,
  output out_5
);

  wire and_1_out, and_2_out, and_3_out, and_4_out, and_5_out, and_6_out, and_7_out, button_1_out, or_1_out,
       or_2_out, or_3_out, t_ff_1_qn, t_ff_2_qn, t_ff_3_qn, t_ff_4_qn;

  Button button_1 (.out(button_1_out));
  and and_1 (and_1_out, t_ff_4_qn, out_4, out_2, t_ff_2_qn);
  or or_1 (or_1_out, and_1_out, and_2_out);
  and and_2 (and_2_out, out_5, out_4, out_3, t_ff_1_qn);
  T_Flip_Flop t_ff_1 (.clk(button_1_out), .T(or_1_out), .Q(out_2), .Qn(t_ff_1_qn), .reset(in_1));  // open: preset, en
  and and_3 (and_3_out, out_5, out_4, t_ff_1_qn);
  T_Flip_Flop t_ff_2 (.clk(button_1_out), .T(and_3_out), .Q(out_3), .Qn(t_ff_2_qn), .reset(in_1));  // open: preset, en
  and and_4 (and_4_out, out_2, t_ff_2_qn, out_4, t_ff_4_qn);
  or or_2 (or_2_out, and_4_out, and_5_out, and_6_out);
  and and_5 (and_5_out, out_5, t_ff_3_qn, t_ff_2_qn, out_2);
  and and_6 (and_6_out, out_5, t_ff_1_qn);
  T_Flip_Flop t_ff_3 (.clk(button_1_out), .T(or_2_out), .Q(out_4), .Qn(t_ff_3_qn), .reset(in_1));  // open: preset, en
  or or_3 (or_3_out, t_ff_1_qn, and_7_out);
  T_Flip_Flop t_ff_4 (.clk(button_1_out), .T(or_3_out), .Q(out_5), .Qn(t_ff_4_qn), .reset(in_1));  // open: preset, en
  and and_7 (and_7_out, t_ff_2_qn, t_ff_3_qn);
endmodule

module counter (
  input  in_1,
  output out_2,
  output out_3,
  output out_4,
  output out_5
);

  wire and_1_out, and_2_out, and_3_out, and_4_out, and_5_out, and_6_out, and_7_out, button_1_out, or_1_out,
       or_2_out, or_3_out, undriven, undriven_2, undriven_3, undriven_4;

  Button button_1 (.out(button_1_out));
  and and_1 (and_1_out, undriven_3, out_4, out_2, undriven_2);
  or or_1 (or_1_out, and_1_out, and_2_out);
  and and_2 (and_2_out, out_5, out_4, out_3, undriven);
  and and_3 (and_3_out, out_5, out_4, undriven);
  and and_4 (and_4_out, out_2, undriven_2, out_4, undriven_3);
  or or_2 (or_2_out, and_4_out, and_5_out, and_6_out);
  and and_5 (and_5_out, out_5, undriven_4, undriven_2, out_2);
  and and_6 (and_6_out, out_5, undriven);
  or or_3 (or_3_out, undriven, and_7_out);
  and and_7 (and_7_out, undriven_2, undriven_4);
endmodule
